// Logisim project GATES.circ as structural Verilog: 1 circuit, main circuit main
module main (
  input  A,
  input  B,
  output Y__AB
);

  xor xor_1 (Y__AB, A, B);

  // Notes on the sheet:
  //   This is XIR gate
endmodule
