// Logisim project Half adder1.circ as structural Verilog: 1 circuit, main circuit main
module main (
  input  A,
  input  B,
  output Y,
  output C
);

  xor xor_1 (Y, A, B);
  and and_1 (C, A, B);

  // Notes on the sheet:
  //   XOR
  //   AND
  //   SUM
  //   OUT
endmodule
