// Logisim project Problem16.circ as structural Verilog: 1 circuit, main circuit main
module main (
  input  A,
  input  B,
  input  in_3,
  input  in_4,
  input  in_5,
  input  in_6,
  input  in_7,
  input  in_8,
  input  in_9,
  input  in_10,
  input  in_11,
  input  in_12,
  output out_13,
  output out_14
);

  wire and_1_out, and_2_out, and_3_out, and_4_out, and_5_out, not_1_out;

  and and_1 (and_1_out, A, B, in_3);
  // OR_Gate or_1 has open pins: in0=in_4, in1=in_5, in2=in_6, out=open
  and and_2 (and_2_out, in_7, in_8);
  and and_3 (and_3_out, in_9, in_10);
  and and_4 (and_4_out, in_11, in_12);
  or or_2 (out_14, and_2_out, and_3_out, and_4_out);
  not not_1 (not_1_out, out_14);
  buf and_5 (and_5_out, not_1_out);  // AND_Gate
  or or_3 (out_13, and_1_out, and_5_out);
endmodule
