// Logisim project Problem3.circ as structural Verilog: 1 circuit, main circuit main
module main (
  input  A,
  input  B,
  input  C,
  output Y
);

  wire and_1_out, not_1_out;

  not not_1 (not_1_out, C);
  and and_1 (and_1_out, A, B);
  and and_2 (Y, and_1_out, B, not_1_out);
endmodule
