// Logisim project SIPO SHIFT REGISTER.circ as structural Verilog: 1 circuit, main circuit main
module main (
  input  D3,
  input  PR,
  input  CLR,
  output Q3,
  output Q2,
  output Q1,
  output Q0
);

  wire clock_1_out;

  Clock clock_1 (.out(clock_1_out));
  D_Flip_Flop d_ff_1 (.clk(clock_1_out), .D(D3), .Q(Q3), .preset(PR), .reset(CLR));  // open: Qn, en
  D_Flip_Flop d_ff_2 (.clk(clock_1_out), .D(Q3), .Q(Q2), .preset(PR), .reset(CLR));  // open: Qn, en
  D_Flip_Flop d_ff_3 (.clk(clock_1_out), .D(Q2), .Q(Q1), .preset(PR), .reset(CLR));  // open: Qn, en
  D_Flip_Flop d_ff_4 (.clk(clock_1_out), .D(Q1), .Q(Q0), .preset(PR), .reset(CLR));  // open: Qn, en

  // Notes on the sheet:
  //   CLK
  //   1011
  //   SIPO SHIFT REGISTER
  //   DFF3
  //   DFF2
  //   DFF1
  //   DFF0
endmodule
