// Logisim project navadeep.circ as structural Verilog: 1 circuit, main circuit main
module main (
  input  in_1,
  input  in_2
);

  wire clock_1_out, NAND_2_out, NAND_3_out, NAND_4_out, NAND_out;

  Clock clock_1 (.out(clock_1_out));
  nand NAND (NAND_out, NAND_4_out, in_1, clock_1_out);
  nand NAND_2 (NAND_2_out, clock_1_out, in_2, NAND_3_out);
  nand NAND_3 (NAND_3_out, NAND_out, NAND_4_out);
  nand NAND_4 (NAND_4_out, NAND_3_out, NAND_2_out);

  // Notes on the sheet:
  //   Q
  //   Q_BAR
endmodule
